# Fritzing sketch Drv8833 Diagram (saved by Fritzing 0.9.3b)
breadboards: 1

parts:
  VCC1 = Battery  # not connected
  VCC2 = Battery
  VCC3 = Battery
  Mod1 = Raspberry Pi Pico
  Part1 = Adafruit DRV8833 DC/Stepper Motor Driver [part_number="Adafruit #3297"]
  M1 = DC Motor
  S1 = Toggle Switch [package=THT]
  R1 = Rotary Potentiometer (Large) [maximum_resistance=100kΩ package=THT]
  VCC4 = Battery

nets:
  N1: VCC2.+, S1.COM
  N2: VCC3.-, Part1.GND
  N3: Mod1.pin_3, Mod1.pin_8, Mod1.pin_13, Mod1.pin_18, Mod1.pin_23, Mod1.pin_28, Mod1.pin_33, Mod1.pin_38, R1.leg1, VCC4.-
  N4: Mod1.pin_19, Part1.AIN2
  N5: Mod1.pin_20, Part1.AIN1
  N6: Mod1.pin_31, R1.wiper
  N7: Mod1.pin_36, R1.leg2
  N8: Mod1.pin_39, VCC4.+
  N9: Part1.AOUT2, M1.pin_1
  N10: Part1.AOUT1, M1.pin_2
  N11: Part1.VMOTOR, S1.L2

custom parts:
  Raspberry Pi Pico: Raspberry Pi Pico. Based around the RP2040 microcontroller the Pico is a low cost microcontroller device bringing Raspberry Pi quality, cost, and easy of use to the microcontroller space. Jan 2021, Split part in to two versions: tht (this one) and SMD. This one will drill holes for a .1 in header in pcb to allow plugging in the module as well as providing pads to solder the module to the top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
  Adafruit DRV8833 DC/Stepper Motor Driver: Spin two DC motors or step one bi-polar or uni-polar stepper with up to 1.2A per channel using the DRV8833. This motor driver chip is a nice alternative to the TB6612 driver. Like that chip, you get 2 full H-bridges, but this chip is better for low voltage uses (can run from 2.7V up to 10.8V motor power) and has built in current limiting capability. We set it up for 1A current limiting so you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
